# Fritzing sketch tower-light (saved by Fritzing 0.9.2b)
circuit board: 8.46667cm x 5.64444cm
stripboards: 1

parts:
  Raspberry_Pi3 = Raspberry Pi 2
  Power_plug_DC_12V2 = Power plug
  U2 = SWITCH-SPST-2 [package=switch-spst-vertical]
  CONN2 = USB connector [package=THT]
  R6 = Resistor [tolerance=±5% resistance=220 package="2010 [SMD]"]
  R7 = Resistor [tolerance=±5% resistance=220 package="2010 [SMD]"]
  R8 = Resistor [tolerance=±5% resistance=220 package="2010 [SMD]"]
  R9 = Resistor [tolerance=±5% resistance=220 package="2010 [SMD]"]
  Q12 = Basic FET N-Channel [package="TO220 [THT]"]
  Q13 = Basic FET N-Channel [package="TO220 [THT]"]
  Q14 = Basic FET N-Channel [package="TO220 [THT]"]
  Q15 = Basic FET N-Channel [package="TO220 [THT]"]
  LED7 = LED - 3mm [color="Red (633nm)" package="3 mm [THT]"]
  LED9 = LED - 3mm [color="Red (633nm)" package="3 mm [THT]"]
  LED10 = LED - 3mm [color="Red (633nm)" package="3 mm [THT]"]
  J2 = Piezo Speaker

nets (from the breadboard view):
  N1: Raspberry_Pi3.GPIO27, R8.Pin_0
  GND: Raspberry_Pi3.GND, Power_plug_DC_12V2.GND, CONN2.GND, CONN2.chassis5, CONN2.chassis6, Q12.source, Q13.source, Q14.source, Q15.source
  N2: Raspberry_Pi3.GPIO24, R9.Pin_0
  N3: Raspberry_Pi3.GPIO23, R7.Pin_0
  N4: Raspberry_Pi3.GPIO18, R6.Pin_0
  N5: Power_plug_DC_12V2.VCC, U2.O
  N6: U2.P, CONN2.5V, LED7.anode, LED9.anode, LED10.anode, J2.pin2
  N7: R6.Pin_1, Q14.gate
  N8: R7.Pin_1, Q13.gate
  N9: R8.Pin_1, Q15.gate
  N10: R9.Pin_1, Q12.gate
  N11: Q12.drain, LED9.cathode
  N12: Q13.drain, J2.pin1
  N13: Q14.drain, LED10.cathode
  N14: Q15.drain, LED7.cathode
